# Fritzing sketch CARSIMU SKETCH (saved by Fritzing 0.9.3b)

parts:
  Composant1 = Bluetooth HC-06
  U1 = SPC56 D Discovery [package=THT]
  L1 = L298
  Q1 = PNP-Transistor [package="TO92 [THT]"]
  M1 = DC Motor  # not connected
  M2 = DC Motor  # not connected

nets:
  N1: Composant1.RXD, U1.PC[6]
  N2: Composant1.TXD, U1.PC[7]
  N3: Composant1.GND, U1.GND#58, Q1.B
  N4: U1.PB[10], L1.Input_2
  5V: U1.5V, L1.+5V, Q1.E
  N5: U1.PA[10], L1.Enable_B
  N6: U1.PB[14], L1.Input_4
  N7: U1.PB[13], L1.Input_3
  N8: U1.PB[12], L1.Input_1
  N9: U1.GND#45, L1.Gnd
  N10: U1.PA[9], L1.Enable_A
  N11: U1.PA[3], Q1.C

notes:
  LM393
  HC06 BT

custom parts:
  SPC56 D Discovery: The SPC560D-DIS discovery board is an evaluation tool supporting STMicroelectronics SPC56 D line microcontrollers. The evaluation board allows full access to all CPUs I/O signals and to peripherals.
  L298: L298 module
